# Fritzing sketch layout (saved by Fritzing 0.9.2b)
breadboards: 1

parts:
  Part1 = Arduino Uno (Rev3)
  R1 = Resistor [tolerance=±5% resistance=10k package=THT]
  R3 = Resistor [tolerance=±5% resistance=100 package=THT]
  IC1 = QFN-20-0.4MM [chip_label="Adafruit SSD1306 128x32 SPI OLED Display" part_number=Adafruit-661 package=QFN]
  S4 = Pushbutton [package="[THT]"]
  S5 = Pushbutton [package="[THT]"]
  R4 = Resistor [tolerance=±5% resistance=10k package=THT]
  J1 = Piezo Speaker

nets:
  N1: Part1.D8, R3.Pin_1
  N2: Part1.D9_PWM, IC1.5
  N3: Part1.D10_PWM/SS, IC1.4
  N4: Part1.D11_PWM/MOSI, IC1.3
  N5: Part1.D12/MISO, IC1.1
  N6: Part1.D13/SCK, IC1.2
  N7: Part1.D6_PWM, Part1.D7, Part1.GND, R1.Pin_1, IC1.8, R4.Pin_1, J1.pin1
  N8: Part1.3V3, IC1.7
  N9: Part1.5V, S4.Pin_3, S4.Pin_4, S5.Pin_3, S5.Pin_4
  N10: R1.Pin_0, S5.Pin_1, S5.Pin_2
  N11: R3.Pin_0, J1.pin2
  N12: S4.Pin_1, S4.Pin_2, R4.Pin_0
